// Logisim project sap1.circ as structural Verilog: 9 circuits, main circuit main
module main (
  output [3:0] out_1,
  output [3:0] out_2
);

  wire [7:0] acumulator_1_to_add_sub;

  ProgramCounter programcounter_1 (.out_5(out_2));  // open: Cp, Clk, Clr, En
  Acumulator acumulator_1 (
    .To_Add_Sub(acumulator_1_to_add_sub), .From_Bus({out_1, out_2}), .To_Bus({out_1, out_2}));  // open: Clk, Clr, nLa, Ea
endmodule

module ProgramCounter (
  input  Cp,
  input  Clk,
  input  Clr,
  input  En,
  output [3:0] out_5
);

  wire halfaddress_1_carry, halfaddress_2_carry, halfaddress_2_soma, halfaddress_3_carry, halfaddress_3_soma,
       halfaddress_4_carry, halfaddress_4_soma, not_1_out;
  wire [3:0] d_ff_4_q;

  not not_1 (not_1_out, Clk);
  HalfAddress halfaddress_1 (.Carry(halfaddress_1_carry), .A(halfaddress_2_carry), .B(d_ff_4_q[3]));  // open: Soma
  D_Flip_Flop d_ff_1 (.clk(not_1_out), .D(halfaddress_1_carry), .Q(d_ff_4_q[3]), .reset(Clr));  // open: Qn, preset, en
  HalfAddress halfaddress_2 (
    .Soma(halfaddress_2_soma), .Carry(halfaddress_2_carry), .A(halfaddress_3_carry), .B(d_ff_4_q[2]));
  D_Flip_Flop d_ff_2 (.clk(not_1_out), .D(halfaddress_2_soma), .Q(d_ff_4_q[2]), .reset(Clr));  // open: Qn, preset, en
  HalfAddress halfaddress_3 (
    .Soma(halfaddress_3_soma), .Carry(halfaddress_3_carry), .A(halfaddress_4_carry), .B(d_ff_4_q[1]));
  D_Flip_Flop d_ff_3 (.clk(not_1_out), .D(halfaddress_3_soma), .Q(d_ff_4_q[1]), .reset(Clr));  // open: Qn, preset, en
  HalfAddress halfaddress_4 (.Soma(halfaddress_4_soma), .Carry(halfaddress_4_carry), .A(Cp), .B(d_ff_4_q[0]));
  D_Flip_Flop d_ff_4 (.clk(not_1_out), .D(halfaddress_4_soma), .Q(d_ff_4_q[0]), .reset(Clr));  // open: Qn, preset, en
  assign out_5 = En ? d_ff_4_q : 4'bz;  // Controlled_Buffer controlled_buffer_1
endmodule

module HalfAddress (
  input  A,
  input  B,
  output Soma,
  output Carry
);

  xor xor_1 (Soma, B, A);
  and and_1 (Carry, A, B);
endmodule

module MAR (
  input  Clk,
  input  Clr,
  input  [3:0] In,
  input  in_4,
  output [3:0] out_5
);

  wire not_1_out;
  wire [3:0] controlled_buffer_1_out;

  assign controlled_buffer_1_out = not_1_out ? In : 4'bz;  // Controlled_Buffer controlled_buffer_1
  not not_1 (not_1_out, in_4);
  D_Flip_Flop d_ff_1 (.clk(Clk), .D(controlled_buffer_1_out[3]), .Q(out_5[3]), .reset(Clr));  // open: Qn, preset, en
  D_Flip_Flop d_ff_2 (.clk(Clk), .D(controlled_buffer_1_out[2]), .Q(out_5[2]), .reset(Clr));  // open: Qn, preset, en
  D_Flip_Flop d_ff_3 (.clk(Clk), .D(controlled_buffer_1_out[1]), .Q(out_5[1]), .reset(Clr));  // open: Qn, preset, en
  D_Flip_Flop d_ff_4 (.clk(Clk), .D(controlled_buffer_1_out[0]), .Q(out_5[0]), .reset(Clr));  // open: Qn, preset, en
endmodule

module Acumulator (
  input  Ea,
  input  Clk,
  input  Clr,
  input  [7:0] From_Bus,
  input  nLa,
  output [7:0] To_Add_Sub,
  output [7:0] To_Bus
);

  wire not_1_out;
  wire [7:0] controlled_buffer_1_out;

  D_Flip_Flop d_ff_1 (
    .clk(Clk), .D(controlled_buffer_1_out[7]), .Q(To_Add_Sub[7]), .reset(Clr));  // open: Qn, preset, en
  D_Flip_Flop d_ff_2 (
    .clk(Clk), .D(controlled_buffer_1_out[6]), .Q(To_Add_Sub[6]), .reset(Clr));  // open: Qn, preset, en
  assign controlled_buffer_1_out = not_1_out ? From_Bus : 8'bz;  // Controlled_Buffer controlled_buffer_1
  not not_1 (not_1_out, nLa);
  D_Flip_Flop d_ff_3 (
    .clk(Clk), .D(controlled_buffer_1_out[5]), .Q(To_Add_Sub[5]), .reset(Clr));  // open: Qn, preset, en
  assign To_Bus = Ea ? To_Add_Sub : 8'bz;  // Controlled_Buffer controlled_buffer_2
  D_Flip_Flop d_ff_4 (
    .clk(Clk), .D(controlled_buffer_1_out[4]), .Q(To_Add_Sub[4]), .reset(Clr));  // open: Qn, preset, en
  D_Flip_Flop d_ff_5 (
    .clk(Clk), .D(controlled_buffer_1_out[3]), .Q(To_Add_Sub[3]), .reset(Clr));  // open: Qn, preset, en
  D_Flip_Flop d_ff_6 (
    .clk(Clk), .D(controlled_buffer_1_out[2]), .Q(To_Add_Sub[2]), .reset(Clr));  // open: Qn, preset, en
  D_Flip_Flop d_ff_7 (
    .clk(Clk), .D(controlled_buffer_1_out[1]), .Q(To_Add_Sub[1]), .reset(Clr));  // open: Qn, preset, en
  D_Flip_Flop d_ff_8 (
    .clk(Clk), .D(controlled_buffer_1_out[0]), .Q(To_Add_Sub[0]), .reset(Clr));  // open: Qn, preset, en
endmodule

module RAM (
  input  [3:0] in_1,
  input  [7:0] in_2,
  input  in_3,
  output [7:0] out_4
);

  wire not_1_out;

  not not_1 (not_1_out, in_3);
  RAM_part #(.addrWidth(4), .bus("separate")) ram_1 (
    .addr(in_1), .din(in_2), .data(out_4), .ld(not_1_out));  // open: str, sel, clk, clr
endmodule

module InstructionDecoder (
  input  I7,
  input  I6,
  input  I5,
  input  I4,
  output Load,
  output Add,
  output Sub,
  output Out,
  output Hlt
);

  wire not_1_out, not_2_out, not_3_out, not_4_out;

  not not_1 (not_1_out, I7);
  not not_2 (not_2_out, I6);
  not not_3 (not_3_out, I4);
  not not_4 (not_4_out, I5);
  and and_1 (Load, I7, not_2_out, I5, I4);
  and and_2 (Add, not_1_out, I6, not_4_out, I4);
  and and_3 (Sub, not_1_out, I6, I5, I4);
  and and_4 (Out, not_1_out, not_2_out, not_4_out, not_3_out);
  and and_5 (Hlt, not_1_out, I6, not_4_out, not_3_out);
endmodule

module RingCounter (
  input  Clk,
  output out_2,
  output out_3,
  output out_4,
  output out_5,
  output out_6,
  output out_7
);

  wire nor_1_out;

  nor nor_1 (nor_1_out, out_2, out_3, out_4, out_5, out_6, out_7);
  D_Flip_Flop d_ff_1 (.clk(Clk), .D(nor_1_out), .Q(out_2));  // open: Qn, preset, en, reset
  D_Flip_Flop d_ff_2 (.clk(Clk), .D(out_2), .Q(out_3));  // open: Qn, preset, en, reset
  D_Flip_Flop d_ff_3 (.clk(Clk), .D(out_3), .Q(out_4));  // open: Qn, preset, en, reset
  D_Flip_Flop d_ff_4 (.clk(Clk), .D(out_4), .Q(out_5));  // open: Qn, preset, en, reset
  D_Flip_Flop d_ff_5 (.clk(Clk), .D(out_5), .Q(out_6));  // open: Qn, preset, en, reset
  D_Flip_Flop d_ff_6 (.clk(Clk), .D(out_6), .Q(out_7));  // open: Qn, preset, en, reset
endmodule

module ControllerSequence (
  input  Clk,
  input  I7,
  input  I6,
  input  I5,
  input  I4,
  output Cp,
  output Ep,
  output nLm,
  output nCE,
  output nLi,
  output nEi,
  output La,
  output Ea,
  output Su,
  output Eu,
  output nLb,
  output nLo,
  output Halt
);

  wire and_1_out, and_2_out, and_3_out, and_4_out, and_5_out, and_6_out, and_7_out, and_8_out, and_9_out,
       and_10_out, and_11_out, and_12_out, and_15_out, and_16_out, and_17_out, and_18_out,
       instructiondecoder_1_add, instructiondecoder_1_load, instructiondecoder_1_out,
       instructiondecoder_1_sub, ringcounter_1_out_4, ringcounter_1_out_5, ringcounter_1_out_6,
       ringcounter_1_out_7;

  InstructionDecoder instructiondecoder_1 (
    .Load(instructiondecoder_1_load), .Add(instructiondecoder_1_add), .Sub(instructiondecoder_1_sub),
    .Out(instructiondecoder_1_out), .Hlt(Halt), .I7(I7), .I6(I6), .I5(I5), .I4(I4));
  RingCounter ringcounter_1 (
    .Clk(Clk), .out_2(Ep), .out_3(Cp), .out_4(ringcounter_1_out_4), .out_5(ringcounter_1_out_5),
    .out_6(ringcounter_1_out_6), .out_7(ringcounter_1_out_7));
  and and_1 (and_1_out, ringcounter_1_out_5, instructiondecoder_1_load);
  and and_2 (and_2_out, ringcounter_1_out_5, instructiondecoder_1_sub);
  and and_3 (and_3_out, ringcounter_1_out_5, instructiondecoder_1_add);
  nor nor_1 (nLm, and_1_out, and_3_out, and_2_out, Ep);
  and and_4 (and_4_out, ringcounter_1_out_6, instructiondecoder_1_load);
  and and_5 (and_5_out, instructiondecoder_1_add, ringcounter_1_out_6);
  nor nor_2 (nCE, and_4_out, and_5_out, and_6_out, ringcounter_1_out_4);
  Hex_Digit_Display hex_digit_display_1 (.value({Cp, Ep, nLm, nCE}));  // open: dp
  and and_6 (and_6_out, instructiondecoder_1_sub, ringcounter_1_out_6);
  not not_1 (nLi, ringcounter_1_out_4);
  and and_7 (and_7_out, ringcounter_1_out_5, instructiondecoder_1_load);
  and and_8 (and_8_out, ringcounter_1_out_5, instructiondecoder_1_add);
  nor nor_3 (nEi, and_7_out, and_8_out, and_9_out);
  and and_9 (and_9_out, ringcounter_1_out_5, instructiondecoder_1_sub);
  and and_10 (and_10_out, ringcounter_1_out_6, instructiondecoder_1_load);
  and and_11 (and_11_out, instructiondecoder_1_sub, ringcounter_1_out_7);
  and and_12 (and_12_out, instructiondecoder_1_add, ringcounter_1_out_7);
  nor nor_4 (La, and_10_out, and_12_out, and_11_out);
  and and_13 (Ea, ringcounter_1_out_5, instructiondecoder_1_out);
  and and_14 (Su, ringcounter_1_out_7, instructiondecoder_1_sub);
  Hex_Digit_Display hex_digit_display_2 (.value({nLi, nEi, La, Ea}));  // open: dp
  and and_15 (and_15_out, ringcounter_1_out_7, instructiondecoder_1_sub);
  and and_16 (and_16_out, ringcounter_1_out_7, instructiondecoder_1_add);
  or or_1 (Eu, and_16_out, and_15_out);
  and and_17 (and_17_out, ringcounter_1_out_6, instructiondecoder_1_sub);
  and and_18 (and_18_out, ringcounter_1_out_6, instructiondecoder_1_add);
  nor nor_5 (nLb, and_18_out, and_17_out);
  nand nand_1 (nLo, instructiondecoder_1_out, ringcounter_1_out_5);
  Hex_Digit_Display hex_digit_display_3 (.value({Su, Eu, nLb, nLo}));  // open: dp
endmodule
